// Logisim project control-logic.circ as structural Verilog: 1 circuit, main circuit control_logic
module control_logic (
  input  [31:0] Instruction,
  input  BrEq,
  input  BrLt,
  output PCSel,
  output RegWEn,
  output [2:0] ImmSel,
  output BrUn,
  output ASel,
  output BSel,
  output [3:0] ALUSel,
  output MemWEn,
  output [1:0] WBSel
);

  wire and_33_out, and_34_out, and_35_out, and_36_out, and_37_out, and_38_out, comparator_1_eq,
       comparator_2_eq, comparator_3_eq, comparator_4_eq, comparator_5_eq, comparator_6_eq, comparator_16_eq,
       comparator_17_eq, comparator_18_eq, comparator_19_eq, comparator_20_eq, comparator_21_eq,
       comparator_22_eq, comparator_23_eq, comparator_24_eq, comparator_25_eq, comparator_26_eq,
       comparator_27_eq, comparator_28_eq, comparator_29_eq, comparator_30_eq, comparator_31_eq,
       comparator_32_eq, comparator_33_eq, comparator_34_eq, comparator_35_eq, comparator_36_eq,
       comparator_37_eq, comparator_38_eq, comparator_39_eq, comparator_40_eq, comparator_41_eq,
       comparator_42_eq, comparator_43_eq, comparator_44_eq, comparator_45_eq, comparator_46_eq,
       comparator_47_eq, comparator_48_eq, comparator_49_eq, comparator_50_eq, comparator_51_eq,
       comparator_52_eq, comparator_53_eq, comparator_54_eq, comparator_55_eq, comparator_56_eq, IType,
       LType, not_1_out, not_2_out, not_3_out, RType, SBType, SType, U0, U1, U2, U3, U4, U5, U6, U7, U8, U9,
       U10, U11, U12, U13, U14, U15, U16, U17, U18, U19, U20, U21, U22, U23, U24, U25, U26, U27, U28, U29,
       U30, U31, U32, U33, U34, U35;
  wire [5:0] multiplexer_1_out, multiplexer_2_out, multiplexer_3_out, multiplexer_4_out, multiplexer_5_out,
       multiplexer_6_out, multiplexer_7_out, multiplexer_8_out, multiplexer_9_out, multiplexer_10_out,
       multiplexer_11_out, multiplexer_12_out, multiplexer_13_out, multiplexer_14_out, multiplexer_15_out,
       multiplexer_16_out, multiplexer_17_out, multiplexer_18_out, multiplexer_19_out, multiplexer_20_out,
       multiplexer_21_out, multiplexer_22_out, multiplexer_23_out, multiplexer_24_out, multiplexer_25_out,
       multiplexer_26_out, multiplexer_27_out, multiplexer_28_out, multiplexer_29_out, multiplexer_30_out,
       multiplexer_31_out, multiplexer_32_out, multiplexer_33_out, multiplexer_34_out, ROMINPUT;
  wire [15:14] rom_1_data;

  Comparator #(.width(3)) comparator_1 (.a(Instruction[14:12]), .b(3'b010), .eq(comparator_1_eq));  // open: gt, lt
  Comparator #(.width(7)) comparator_2 (.a(Instruction[31:25]), .b({7{1'b0}}), .eq(comparator_2_eq));  // open: gt, lt
  Comparator #(.width(3)) comparator_3 (.a(Instruction[14:12]), .b(3'b100), .eq(comparator_3_eq));  // open: gt, lt
  Comparator #(.width(7)) comparator_4 (.a(Instruction[31:25]), .b({7{1'b0}}), .eq(comparator_4_eq));  // open: gt, lt
  Comparator #(.width(3)) comparator_5 (.a(Instruction[14:12]), .b(3'b101), .eq(comparator_5_eq));  // open: gt, lt
  Comparator #(.width(7)) comparator_6 (.a(Instruction[31:25]), .b({7{1'b0}}), .eq(comparator_6_eq));  // open: gt, lt
  Comparator #(.width(7)) comparator_7 (.a(Instruction[6:0]), .b(7'b0110011), .eq(RType));  // open: gt, lt
  Comparator #(.width(7)) comparator_8 (.a(Instruction[6:0]), .b(7'b0000011), .eq(LType));  // open: gt, lt
  Comparator #(.width(7)) comparator_9 (.a(Instruction[6:0]), .b(7'b0010011), .eq(IType));  // open: gt, lt
  Comparator #(.width(7)) comparator_10 (.a(Instruction[6:0]), .b(7'b0100011), .eq(SType));  // open: gt, lt
  Comparator #(.width(7)) comparator_11 (.a(Instruction[6:0]), .b(7'b1100011), .eq(SBType));  // open: gt, lt
  Comparator #(.width(7)) comparator_12 (.a(Instruction[6:0]), .b(7'b0010111), .eq(U32));  // open: gt, lt
  Comparator #(.width(7)) comparator_13 (.a(Instruction[6:0]), .b(7'b0110111), .eq(U33));  // open: gt, lt
  Comparator #(.mode("unsigned"), .width(7)) comparator_14 (
    .a(Instruction[6:0]), .b(7'b1101111), .eq(U34));  // open: gt, lt
  Comparator #(.mode("unsigned"), .width(7)) comparator_15 (
    .a(Instruction[6:0]), .b(7'b1100111), .eq(U35));  // open: gt, lt
  Comparator #(.width(3)) comparator_16 (.a(Instruction[14:12]), .b(3'b101), .eq(comparator_16_eq));  // open: gt, lt
  Comparator #(.width(7)) comparator_17 (
    .a(Instruction[31:25]), .b(7'b0100000), .eq(comparator_17_eq));  // open: gt, lt
  Comparator #(.width(3)) comparator_18 (.a(Instruction[14:12]), .b(3'b110), .eq(comparator_18_eq));  // open: gt, lt
  Comparator #(.width(7)) comparator_19 (.a(Instruction[31:25]), .b({7{1'b0}}), .eq(comparator_19_eq));  // open: gt, lt
  Comparator #(.width(3)) comparator_20 (.a(Instruction[14:12]), .b(3'b111), .eq(comparator_20_eq));  // open: gt, lt
  Comparator #(.width(7)) comparator_21 (.a(Instruction[31:25]), .b({7{1'b0}}), .eq(comparator_21_eq));  // open: gt, lt
  Comparator #(.width(3)) comparator_22 (.a(Instruction[14:12]), .b(3'b000), .eq(comparator_22_eq));  // open: gt, lt
  Comparator #(.width(3)) comparator_23 (.a(Instruction[14:12]), .b(3'b001), .eq(comparator_23_eq));  // open: gt, lt
  Comparator #(.width(3)) comparator_24 (.a(Instruction[14:12]), .b(3'b010), .eq(comparator_24_eq));  // open: gt, lt
  Comparator #(.width(3)) comparator_25 (.a(Instruction[14:12]), .b(3'b000), .eq(comparator_25_eq));  // open: gt, lt
  Comparator #(.width(3)) comparator_26 (.a(Instruction[14:12]), .b(3'b001), .eq(comparator_26_eq));  // open: gt, lt
  Comparator #(.width(3)) comparator_27 (.a(Instruction[14:12]), .b(3'b010), .eq(comparator_27_eq));  // open: gt, lt
  Comparator #(.width(3)) comparator_28 (.a(Instruction[14:12]), .b(3'b000), .eq(comparator_28_eq));  // open: gt, lt
  Comparator #(.width(3)) comparator_29 (.a(Instruction[14:12]), .b(3'b001), .eq(comparator_29_eq));  // open: gt, lt
  Comparator #(.width(3)) comparator_30 (.a(Instruction[14:12]), .b(3'b100), .eq(comparator_30_eq));  // open: gt, lt
  Comparator #(.width(3)) comparator_31 (.a(Instruction[14:12]), .b(3'b101), .eq(comparator_31_eq));  // open: gt, lt
  Comparator #(.width(3)) comparator_32 (.a(Instruction[14:12]), .b(3'b110), .eq(comparator_32_eq));  // open: gt, lt
  Comparator #(.width(3)) comparator_33 (.a(Instruction[14:12]), .b(3'b111), .eq(comparator_33_eq));  // open: gt, lt
  ROM #(.addrWidth(6), .dataWidth(16)) rom_1 (
    .addr(ROMINPUT), .data({rom_1_data, WBSel, MemWEn, ALUSel, BSel, ASel, BrUn, ImmSel, RegWEn}));
  and and_1 (U6, RType, comparator_1_eq, comparator_2_eq);
  and and_2 (U7, RType, comparator_3_eq, comparator_4_eq);
  and and_3 (U8, RType, comparator_5_eq, comparator_6_eq);
  and and_4 (U9, RType, comparator_16_eq, comparator_17_eq);
  and and_5 (U10, RType, comparator_18_eq, comparator_19_eq);
  and and_6 (U11, RType, comparator_20_eq, comparator_21_eq);
  and and_7 (U12, LType, comparator_22_eq);
  and and_8 (U13, LType, comparator_23_eq);
  and and_9 (U14, LType, comparator_24_eq);
  and and_10 (U23, SType, comparator_25_eq);
  and and_11 (U24, SType, comparator_26_eq);
  and and_12 (U25, SType, comparator_27_eq);
  and and_13 (U26, SBType, comparator_28_eq);
  and and_14 (U27, SBType, comparator_29_eq);
  and and_15 (U28, SBType, comparator_30_eq);
  and and_16 (U29, SBType, comparator_31_eq);
  and and_17 (U30, SBType, comparator_32_eq);
  and and_18 (U31, SBType, comparator_33_eq);
  Comparator #(.width(3)) comparator_34 (.a(Instruction[14:12]), .b(3'b000), .eq(comparator_34_eq));  // open: gt, lt
  Comparator #(.width(7)) comparator_35 (.a(Instruction[31:25]), .b({7{1'b0}}), .eq(comparator_35_eq));  // open: gt, lt
  Comparator #(.width(3)) comparator_36 (.a(Instruction[14:12]), .b(3'b000), .eq(comparator_36_eq));  // open: gt, lt
  Comparator #(.width(7)) comparator_37 (
    .a(Instruction[31:25]), .b(7'b0000001), .eq(comparator_37_eq));  // open: gt, lt
  Comparator #(.width(3)) comparator_38 (.a(Instruction[14:12]), .b(3'b000), .eq(comparator_38_eq));  // open: gt, lt
  Comparator #(.width(7)) comparator_39 (
    .a(Instruction[31:25]), .b(7'b0100000), .eq(comparator_39_eq));  // open: gt, lt
  Comparator #(.width(3)) comparator_40 (.a(Instruction[14:12]), .b(3'b001), .eq(comparator_40_eq));  // open: gt, lt
  Comparator #(.width(7)) comparator_41 (.a(Instruction[31:25]), .b({7{1'b0}}), .eq(comparator_41_eq));  // open: gt, lt
  Comparator #(.width(3)) comparator_42 (.a(Instruction[14:12]), .b(3'b001), .eq(comparator_42_eq));  // open: gt, lt
  Comparator #(.width(7)) comparator_43 (
    .a(Instruction[31:25]), .b(7'b0000001), .eq(comparator_43_eq));  // open: gt, lt
  Comparator #(.width(3)) comparator_44 (.a(Instruction[14:12]), .b(3'b011), .eq(comparator_44_eq));  // open: gt, lt
  Comparator #(.width(7)) comparator_45 (
    .a(Instruction[31:25]), .b(7'b0000001), .eq(comparator_45_eq));  // open: gt, lt
  Comparator #(.width(3)) comparator_46 (.a(Instruction[14:12]), .b(3'b000), .eq(comparator_46_eq));  // open: gt, lt
  Comparator #(.width(3)) comparator_47 (.a(Instruction[14:12]), .b(3'b001), .eq(comparator_47_eq));  // open: gt, lt
  Comparator #(.width(7)) comparator_48 (.a(Instruction[31:25]), .b({7{1'b0}}), .eq(comparator_48_eq));  // open: gt, lt
  Comparator #(.width(3)) comparator_49 (.a(Instruction[14:12]), .b(3'b010), .eq(comparator_49_eq));  // open: gt, lt
  Comparator #(.width(3)) comparator_50 (.a(Instruction[14:12]), .b(3'b100), .eq(comparator_50_eq));  // open: gt, lt
  Comparator #(.width(3)) comparator_51 (.a(Instruction[14:12]), .b(3'b101), .eq(comparator_51_eq));  // open: gt, lt
  Comparator #(.width(7)) comparator_52 (.a(Instruction[31:25]), .b({7{1'b0}}), .eq(comparator_52_eq));  // open: gt, lt
  Comparator #(.width(3)) comparator_53 (.a(Instruction[14:12]), .b(3'b101), .eq(comparator_53_eq));  // open: gt, lt
  Comparator #(.width(7)) comparator_54 (
    .a(Instruction[31:25]), .b(7'b0100000), .eq(comparator_54_eq));  // open: gt, lt
  Comparator #(.width(3)) comparator_55 (.a(Instruction[14:12]), .b(3'b110), .eq(comparator_55_eq));  // open: gt, lt
  Comparator #(.width(3)) comparator_56 (.a(Instruction[14:12]), .b(3'b111), .eq(comparator_56_eq));  // open: gt, lt
  and and_19 (U0, RType, comparator_34_eq, comparator_35_eq);
  and and_20 (U1, RType, comparator_36_eq, comparator_37_eq);
  and and_21 (U2, RType, comparator_38_eq, comparator_39_eq);
  and and_22 (U3, RType, comparator_40_eq, comparator_41_eq);
  and and_23 (U4, RType, comparator_42_eq, comparator_43_eq);
  and and_24 (U5, RType, comparator_44_eq, comparator_45_eq);
  and and_25 (U15, IType, comparator_46_eq, 1'b1);
  and and_26 (U16, IType, comparator_47_eq, comparator_48_eq);
  and and_27 (U17, IType, comparator_49_eq, 1'b1);
  and and_28 (U18, IType, comparator_50_eq, 1'b1);
  and and_29 (U19, IType, comparator_51_eq, comparator_52_eq);
  and and_30 (U20, IType, comparator_53_eq, comparator_54_eq);
  and and_31 (U21, IType, comparator_55_eq);
  and and_32 (U22, IType, comparator_56_eq);
  not not_1 (not_1_out, BrEq);
  not not_2 (not_2_out, BrLt);
  and and_33 (and_33_out, U26, BrEq);
  and and_34 (and_34_out, U27, not_1_out);
  and and_35 (and_35_out, U28, BrLt);
  and and_36 (and_36_out, U29, not_2_out);
  and and_37 (and_37_out, U30, BrLt);
  not not_3 (not_3_out, BrLt);
  and and_38 (and_38_out, U31, not_3_out);
  or or_1 (PCSel, U34, and_33_out, and_34_out, and_35_out, and_36_out, and_37_out, and_38_out, U35);
  Multiplexer #(.enable("false"), .width(6)) multiplexer_1 (
    .in0({6{1'b0}}), .in1(6'b000001), .out(multiplexer_1_out), .sel(U1));
  Multiplexer #(.enable("false"), .width(6)) multiplexer_2 (
    .in0(multiplexer_31_out), .in1(6'b001000), .out(multiplexer_2_out), .sel(U8));
  Multiplexer #(.enable("false"), .width(6)) multiplexer_3 (
    .in0(multiplexer_32_out), .in1(6'b001111), .out(multiplexer_3_out), .sel(U15));
  Multiplexer #(.enable("false"), .width(6)) multiplexer_4 (
    .in0(multiplexer_33_out), .in1(6'b010110), .out(multiplexer_4_out), .sel(U22));
  Multiplexer #(.enable("false"), .width(6)) multiplexer_5 (
    .in0(multiplexer_34_out), .in1(6'b011101), .out(multiplexer_5_out), .sel(U29));
  Multiplexer #(.enable("false"), .width(6)) multiplexer_6 (
    .in0(multiplexer_1_out), .in1(6'b000010), .out(multiplexer_6_out), .sel(U2));
  Multiplexer #(.enable("false"), .width(6)) multiplexer_7 (
    .in0(multiplexer_6_out), .in1(6'b000011), .out(multiplexer_7_out), .sel(U3));
  Multiplexer #(.enable("false"), .width(6)) multiplexer_8 (
    .in0(multiplexer_2_out), .in1(6'b001001), .out(multiplexer_8_out), .sel(U9));
  Multiplexer #(.enable("false"), .width(6)) multiplexer_9 (
    .in0(multiplexer_8_out), .in1(6'b001010), .out(multiplexer_9_out), .sel(U10));
  Multiplexer #(.enable("false"), .width(6)) multiplexer_10 (
    .in0(multiplexer_3_out), .in1(6'b010000), .out(multiplexer_10_out), .sel(U16));
  Multiplexer #(.enable("false"), .width(6)) multiplexer_11 (
    .in0(multiplexer_10_out), .in1(6'b010001), .out(multiplexer_11_out), .sel(U17));
  Multiplexer #(.enable("false"), .width(6)) multiplexer_12 (
    .in0(multiplexer_4_out), .in1(6'b010111), .out(multiplexer_12_out), .sel(U23));
  Multiplexer #(.enable("false"), .width(6)) multiplexer_13 (
    .in0(multiplexer_12_out), .in1(6'b011000), .out(multiplexer_13_out), .sel(U24));
  Multiplexer #(.enable("false"), .width(6)) multiplexer_14 (
    .in0(multiplexer_5_out), .in1(6'b011110), .out(multiplexer_14_out), .sel(U30));
  Multiplexer #(.enable("false"), .width(6)) multiplexer_15 (
    .in0(multiplexer_7_out), .in1(6'b000100), .out(multiplexer_15_out), .sel(U4));
  Multiplexer #(.enable("false"), .width(6)) multiplexer_16 (
    .in0(multiplexer_9_out), .in1(6'b001011), .out(multiplexer_16_out), .sel(U11));
  Multiplexer #(.enable("false"), .width(6)) multiplexer_17 (
    .in0(multiplexer_11_out), .in1(6'b010010), .out(multiplexer_17_out), .sel(U18));
  Multiplexer #(.enable("false"), .width(6)) multiplexer_18 (
    .in0(multiplexer_13_out), .in1(6'b011001), .out(multiplexer_18_out), .sel(U25));
  Multiplexer #(.enable("false"), .width(6)) multiplexer_19 (
    .in0(multiplexer_14_out), .in1(6'b011111), .out(multiplexer_19_out), .sel(U31));
  Multiplexer #(.enable("false"), .width(6)) multiplexer_20 (
    .in0(multiplexer_19_out), .in1(6'b100000), .out(multiplexer_20_out), .sel(U32));
  Multiplexer #(.enable("false"), .width(6)) multiplexer_21 (
    .in0(multiplexer_15_out), .in1(6'b000101), .out(multiplexer_21_out), .sel(U5));
  Multiplexer #(.enable("false"), .width(6)) multiplexer_22 (
    .in0(multiplexer_16_out), .in1(6'b001100), .out(multiplexer_22_out), .sel(U12));
  Multiplexer #(.enable("false"), .width(6)) multiplexer_23 (
    .in0(multiplexer_17_out), .in1(6'b010011), .out(multiplexer_23_out), .sel(U19));
  Multiplexer #(.enable("false"), .width(6)) multiplexer_24 (
    .in0(multiplexer_18_out), .in1(6'b011010), .out(multiplexer_24_out), .sel(U26));
  Multiplexer #(.enable("false"), .width(6)) multiplexer_25 (
    .in0(multiplexer_20_out), .in1(6'b100001), .out(multiplexer_25_out), .sel(U33));
  Multiplexer #(.enable("false"), .width(6)) multiplexer_26 (
    .in0(multiplexer_21_out), .in1(6'b000110), .out(multiplexer_26_out), .sel(U6));
  Multiplexer #(.enable("false"), .width(6)) multiplexer_27 (
    .in0(multiplexer_22_out), .in1(6'b001101), .out(multiplexer_27_out), .sel(U13));
  Multiplexer #(.enable("false"), .width(6)) multiplexer_28 (
    .in0(multiplexer_23_out), .in1(6'b010100), .out(multiplexer_28_out), .sel(U20));
  Multiplexer #(.enable("false"), .width(6)) multiplexer_29 (
    .in0(multiplexer_24_out), .in1(6'b011011), .out(multiplexer_29_out), .sel(U27));
  Multiplexer #(.enable("false"), .width(6)) multiplexer_30 (
    .in0(multiplexer_25_out), .in1(6'b100010), .out(multiplexer_30_out), .sel(U34));
  Multiplexer #(.enable("false"), .width(6)) multiplexer_31 (
    .in0(multiplexer_26_out), .in1(6'b000111), .out(multiplexer_31_out), .sel(U7));
  Multiplexer #(.enable("false"), .width(6)) multiplexer_32 (
    .in0(multiplexer_27_out), .in1(6'b001110), .out(multiplexer_32_out), .sel(U14));
  Multiplexer #(.enable("false"), .width(6)) multiplexer_33 (
    .in0(multiplexer_28_out), .in1(6'b010101), .out(multiplexer_33_out), .sel(U21));
  Multiplexer #(.enable("false"), .width(6)) multiplexer_34 (
    .in0(multiplexer_29_out), .in1(6'b011100), .out(multiplexer_34_out), .sel(U28));
  Multiplexer #(.enable("false"), .width(6)) multiplexer_35 (
    .in0(multiplexer_30_out), .in1(6'b100011), .out(ROMINPUT), .sel(U35));

  // Other names for the same wires on the sheet: OPCODE[6:0] = Instruction[6:0]; func3[2:0] = Instruction[14:12];
  //   func7[6:0] = Instruction[31:25]

  // Notes on the sheet:
  //   INPUTS to your circuit
  //   Connect ROM Input here ->
  //   contents of rom_1 (hex, n*v repeats v):
  //   1001 1401 1601 1081 1481 1581 1101 1201 1281 1681 1301 1381 41 41 41 1041 10c1 1141 1241 12c1 16c1
  //   1341 13c1 1842 1842 1842 4*1064 1074 1074 1067 3067 2069 2041
  //   ROM FOR CONTROL LOGIC
  //   DON'T CHANGE THE LOCATIONS OF THE INPUTS AND OUTPUTS!
  //   This is only if you choose to do the ROM option
  //   CONNECT
  //   WIRE
  //   TO
  //   USE
  //   ROM
  //   OUTPUT from your circuit
  //   Reminder: If using ROM, use combinational logic for PCSel
endmodule
