// Logisim project cpu.circ as structural Verilog: 1 circuit, main circuit cpu
module cpu (
  input  clk,
  input  [31:0] Instruction,
  input  [31:0] MemReadData,
  output [31:0] MemAddress,
  output [31:0] ProgramCounter,
  output [31:0] ra,
  output [31:0] sp,
  output [31:0] t0,
  output [31:0] t1,
  output [31:0] t2,
  output [31:0] s0,
  output [31:0] s1,
  output [31:0] a0,
  output [3:0] MemWriteMask,
  output [31:0] MemWriteData
);

  wire ASel, BrEq, BrLt, BrUn, BSel, MenWEn, PCSel, RegWEn;
  wire [1:0] WBSel;
  wire [2:0] funct3, ImmSel;
  wire [3:0] ALUSel;
  wire [31:0] DatatoReg, imm, InstructionQ, multiplexer_1_out, multiplexer_2_out, multiplexer_3_out,
       multiplexer_4_out, PC4, PC_F, PC_F4, RegReadData1, RegReadData2, WBVAL;

  Adder #(.width(32)) adder_1 (.a(ProgramCounter), .b(32'h4), .out(PC4));  // open: cin, cout
  Register #(.width(32)) PC (.D(multiplexer_1_out), .clk(clk), .Q(ProgramCounter));  // open: en, clr
  Multiplexer #(.enable("false"), .width(32)) multiplexer_1 (
    .in0(PC4), .in1(MemAddress), .out(multiplexer_1_out), .sel(PCSel));
  Multiplexer #(.enable("false"), .width(32)) multiplexer_2 (
    .in0(Instruction), .in1(32'h13), .out(multiplexer_2_out), .sel(PCSel));
  Register #(.width(32)) register_1 (
    .D(multiplexer_2_out), .clk(clk), .Q({InstructionQ[31:15], funct3, InstructionQ[11:0]}));  // open: en, clr
  Register #(.width(32)) register_2 (.D(ProgramCounter), .clk(clk), .Q(PC_F));  // open: en, clr
  Adder #(.width(32)) adder_2 (.a(PC_F), .b(32'h4), .out(PC_F4));  // open: cin, cout
  control_logic control_logic_1 (
    .PCSel(PCSel), .RegWEn(RegWEn), .ImmSel(ImmSel), .BrUn(BrUn), .ASel(ASel), .BSel(BSel), .ALUSel(ALUSel),
    .MemWEn(MenWEn), .WBSel(WBSel), .Instruction({InstructionQ[31:15], funct3, InstructionQ[11:0]}),
    .BrEq(BrEq), .BrLt(BrLt));
  regfile regfile_1 (
    .rs1(InstructionQ[19:15]), .rs2(InstructionQ[24:20]), .rd(InstructionQ[11:7]), .Write_Data(WBVAL),
    .RegWEn(RegWEn), .clk(clk), .ra(ra), .sp(sp), .t0(t0), .t1(t1), .t2(t2), .s0(s0), .s1(s1), .a0(a0),
    .Read_Data_1(RegReadData1), .Read_Data_2(RegReadData2));
  // imm_gen imm_gen_1: pin names not known; wires that end beside it: {InstructionQ[31:15], funct3, InstructionQ[11:0]}, ImmSel, imm
  Multiplexer #(.enable("false"), .width(32)) multiplexer_3 (
    .in0(RegReadData1), .in1(PC_F), .out(multiplexer_3_out), .sel(ASel));
  Multiplexer #(.enable("false"), .width(32)) multiplexer_4 (
    .in0(RegReadData2), .in1(imm), .out(multiplexer_4_out), .sel(BSel));
  alu alu_1 (.Result(MemAddress), .A(multiplexer_3_out), .B(multiplexer_4_out), .ALUSel(ALUSel));  // open: out_5
  branch_comp branch_comp_1 (.BrData1(RegReadData1), .BrData2(RegReadData2), .BrUn(BrUn), .BrEq(BrEq), .BrLt(BrLt));
  Multiplexer #(.enable("false"), .select(2), .width(32)) multiplexer_5 (
    .in0(DatatoReg), .in1(MemAddress), .in2(PC_F4), .in3(imm), .out(WBVAL), .sel(WBSel));
  partial_store partial_store_1 (
    .Instruction({InstructionQ[31:15], funct3, InstructionQ[11:0]}), .MemAddress(MemAddress),
    .DataFromReg(RegReadData2), .MemWEn(MenWEn), .MemWriteMask(MemWriteMask), .DataToMem(MemWriteData));
  partial_load partial_load_1 (
    .Instruction({InstructionQ[31:15], funct3, InstructionQ[11:0]}), .MemAddress(MemAddress),
    .DataFromMem(MemReadData), .DataToReg(DatatoReg));

  // Other names for the same wires on the sheet: ALUResult[31:0] = MemAddress; opcode[6:0] = InstructionQ[6:0];
  //   rd[4:0] = InstructionQ[11:7]; InstructionQ[14:12] = funct3; rs1[4:0] = InstructionQ[19:15];
  //   rs2[4:0] = InstructionQ[24:20]

  // Notes on the sheet:
  //   To IMEM
  //   IMEM (do **NOT** move this)
  //   From IMEM
  //   Inputs/Outputs for testing. Do **NOT** move these.
  //   It is OK to move the PC, RegFile, ALU, MEM, Branch Comp, Imm Gen, Partial Load, Partial Store and Control Logic to wherever is most convenient for you when constructing your CPU, and to delete this text
  //   To DMEM
  //   DMEM (do **NOT** move this)
  //   From DMEM
endmodule
