// Logisim project partial-load.circ as structural Verilog: 1 circuit, main circuit partial_load
module partial_load (
  input  [31:0] Instruction,
  input  [31:0] MemAddress,
  input  [31:0] DataFromMem,
  output [31:0] DataToReg
);

  wire lb, lh, lw;
  wire [7:0] multiplexer_2_out;
  wire [15:0] multiplexer_4_out, multiplexer_5_out, undriven;
  wire [23:0] multiplexer_1_out;
  wire [31:0] multiplexer_3_out, multiplexer_6_out;

  Comparator #(.width(3)) comparator_1 (.a(Instruction[14:12]), .b(3'b000), .eq(lb));  // open: gt, lt
  Comparator #(.width(3)) comparator_2 (.a(Instruction[14:12]), .b(3'b001), .eq(lh));  // open: gt, lt
  Comparator #(.width(3)) comparator_3 (.a(Instruction[14:12]), .b(3'b010), .eq(lw));  // open: gt, lt
  Multiplexer #(.enable("false"), .width(24)) multiplexer_1 (
    .in0({24{1'b0}}), .in1({24{1'b1}}), .out(multiplexer_1_out), .sel(DataFromMem[31]));
  Multiplexer #(.enable("false"), .select(2), .width(8)) multiplexer_2 (
    .in0(DataFromMem[7:0]), .in1(DataFromMem[15:8]), .in2(DataFromMem[23:16]), .in3(DataFromMem[31:24]),
    .out(multiplexer_2_out), .sel(MemAddress[1:0]));
  Multiplexer #(.enable("false"), .width(32)) multiplexer_3 (
    .in0({32{1'b0}}), .in1({multiplexer_1_out, multiplexer_2_out}), .out(multiplexer_3_out), .sel(lb));
  Multiplexer #(.enable("false"), .width(16)) multiplexer_4 (
    .in0({16{1'b0}}), .in1({16{1'b1}}), .out(multiplexer_4_out), .sel(DataFromMem[31]));
  Multiplexer #(.enable("false"), .select(2), .width(16)) multiplexer_5 (
    .in0(DataFromMem[15:0]), .in1(DataFromMem[23:8]), .in2(DataFromMem[31:16]), .in3(undriven),
    .out(multiplexer_5_out), .sel(MemAddress[1:0]));
  Multiplexer #(.enable("false"), .width(32)) multiplexer_6 (
    .in0(multiplexer_3_out), .in1({multiplexer_4_out, multiplexer_5_out}), .out(multiplexer_6_out), .sel(lh));
  Multiplexer #(.enable("false"), .width(32)) multiplexer_7 (
    .in0(multiplexer_6_out), .in1(DataFromMem), .out(DataToReg), .sel(lw));

  // Other names for the same wires on the sheet: p07[7:0] = DataFromMem[7:0]; p015[15:0] = DataFromMem[15:0];
  //   p815[7:0] = DataFromMem[15:8]; p823[15:0] = DataFromMem[23:8]; p1623[7:0] = DataFromMem[23:16];
  //   p1631[15:0] = DataFromMem[31:16]; p2431[7:0] = DataFromMem[31:24]; Sign = DataFromMem[31];
  //   func3[2:0] = Instruction[14:12]; low2bit[1:0] = MemAddress[1:0]

  // Notes on the sheet:
  //   INPUTS to your circuit
  //   DON'T CHANGE THE LOCATIONS OF THE INPUTS AND OUTPUTS!
  //   OUTPUT from your circuit
endmodule
