// Logisim project partial-store.circ as structural Verilog: 1 circuit, main circuit partial_store
module partial_store (
  input  [31:0] Instruction,
  input  [31:0] MemAddress,
  input  [31:0] DataFromReg,
  input  MemWEn,
  output [3:0] MemWriteMask,
  output [31:0] DataToMem
);

  wire sb, sh, sw;
  wire [3:0] multiplexer_4_out, multiplexer_5_out, multiplexer_6_out, multiplexer_8_out, multiplexer_9_out;
  wire [31:0] multiplexer_1_out, multiplexer_2_out, multiplexer_3_out, multiplexer_7_out, undriven;

  Comparator #(.width(3)) comparator_1 (.a(Instruction[14:12]), .b(3'b000), .eq(sb));  // open: gt, lt
  Comparator #(.width(3)) comparator_2 (.a(Instruction[14:12]), .b(3'b001), .eq(sh));  // open: gt, lt
  Comparator #(.width(3)) comparator_3 (.a(Instruction[14:12]), .b(3'b010), .eq(sw));  // open: gt, lt
  Multiplexer #(.enable("false"), .select(2), .width(32)) multiplexer_1 (
    .in0({{24{1'b0}}, DataFromReg[7:0]}), .in1({{16{1'b0}}, DataFromReg[7:0], {8{1'b0}}}),
    .in2({{8{1'b0}}, DataFromReg[7:0], {16{1'b0}}}), .in3({DataFromReg[7:0], {24{1'b0}}}),
    .out(multiplexer_1_out), .sel(MemAddress[1:0]));
  Multiplexer #(.enable("false"), .width(32)) multiplexer_2 (
    .in0({32{1'b0}}), .in1(multiplexer_1_out), .out(multiplexer_2_out), .sel(sb));
  Multiplexer #(.enable("false"), .select(2), .width(32)) multiplexer_3 (
    .in0({{16{1'b0}}, DataFromReg[15:0]}), .in2({DataFromReg[15:0], {16{1'b0}}}), .in3(undriven),
    .out(multiplexer_3_out), .sel(MemAddress[1:0]));  // open: in1
  Multiplexer #(.enable("false"), .width(4)) multiplexer_4 (
    .in0(4'b0000), .in1(multiplexer_5_out), .out(multiplexer_4_out), .sel(sb));
  Multiplexer #(.enable("false"), .select(2), .width(4)) multiplexer_5 (
    .in0(4'b0001), .in1(4'b0010), .in2(4'b0100), .in3(4'b1000), .out(multiplexer_5_out), .sel(MemAddress[1:0]));
  Multiplexer #(.enable("false"), .select(2), .width(4)) multiplexer_6 (
    .in0(4'b0011), .in2(4'b1100), .out(multiplexer_6_out), .sel(MemAddress[1:0]));  // open: in1, in3
  Multiplexer #(.enable("false"), .width(32)) multiplexer_7 (
    .in0(multiplexer_2_out), .in1(multiplexer_3_out), .out(multiplexer_7_out), .sel(sh));
  Multiplexer #(.enable("false"), .width(4)) multiplexer_8 (
    .in0(multiplexer_4_out), .in1(multiplexer_6_out), .out(multiplexer_8_out), .sel(sh));
  Multiplexer #(.enable("false"), .width(4)) multiplexer_9 (
    .in0(multiplexer_8_out), .in1(4'b1111), .out(multiplexer_9_out), .sel(sw));
  Multiplexer #(.enable("false"), .width(32)) multiplexer_10 (
    .in0(multiplexer_7_out), .in1(DataFromReg), .out(DataToMem), .sel(sw));
  Multiplexer #(.enable("false"), .width(4)) multiplexer_11 (
    .in0(4'b0000), .in1(multiplexer_9_out), .out(MemWriteMask), .sel(MemWEn));

  // Other names for the same wires on the sheet: p07[7:0] = DataFromReg[7:0]; p015[15:0] = DataFromReg[15:0];
  //   p815[7:0] = DataFromReg[15:8]; p823[15:0] = DataFromReg[23:8]; p1623[7:0] = DataFromReg[23:16];
  //   p1631[15:0] = DataFromReg[31:16]; p2431[7:0] = DataFromReg[31:24]; Sign = DataFromReg[31];
  //   func3[2:0] = Instruction[14:12]; low2bit[1:0] = MemAddress[1:0]

  // Notes on the sheet:
  //   INPUTS to your circuit
  //   DON'T CHANGE THE LOCATIONS OF THE INPUTS AND OUTPUTS!
  //   OUTPUT from your circuit
endmodule
