// Logisim project cpuLast.circ as structural Verilog: 1 circuit, main circuit cpu
module cpu (
  input  clk,
  input  [31:0] INSTRUCTION,
  input  [31:0] MEM_READ_DATA,
  output [31:0] MEM_WRITE_ADDRESS,
  output [31:0] PROGRAM_COUNTER,
  output [31:0] ra,
  output [31:0] sp,
  output [31:0] t0,
  output [31:0] t1,
  output [31:0] t2,
  output [31:0] s0,
  output [31:0] s1,
  output [31:0] a0,
  output [31:0] tohost,
  output [3:0] MEM_WRITE_ENABLE,
  output [31:0] MEM_WRITE_DATA
);

  wire ASel, BrEq, BrLt, BrUn, BSel, comparator_1_eq, comparator_2_eq, comparator_3_eq, comparator_4_eq,
       comparator_5_eq, comparator_6_eq, comparator_7_eq, comparator_8_eq, CSRSel, CSRWE, lb, lh, lw, MemRW,
       PCSel, RegWEn, sb, sh, sw;
  wire [1:0] WBSel;
  wire [2:0] ImmSel;
  wire [3:0] ALUSel, multiplexer_6_out, multiplexer_7_out, multiplexer_8_out, multiplexer_11_out,
       multiplexer_13_out;
  wire [7:0] multiplexer_9_out;
  wire [15:0] multiplexer_12_out;
  wire [31:0] csr_din, data_lh, data_sh, imm, MEM_WRITE_reg, multiplexer_1_out, multiplexer_3_out,
       multiplexer_4_out, multiplexer_14_out, multiplexer_15_out, multiplexer_17_out, multiplexer_19_out,
       pc_4, read_data_1, read_mem, wb_data;

  Adder #(.width(32)) adder_1 (.a(PROGRAM_COUNTER), .b(32'h4), .out(pc_4));  // open: cin, cout
  Register #(.width(32)) PC (.D(multiplexer_1_out), .clk(clk), .Q(PROGRAM_COUNTER));  // open: en, clr
  Multiplexer #(.enable("false"), .width(32)) multiplexer_1 (
    .in0(pc_4), .in1(MEM_WRITE_ADDRESS), .out(multiplexer_1_out), .sel(PCSel));
  // imm_gen imm_gen_1: pin names not known; wires that end beside it: INSTRUCTION, ImmSel, imm
  // control_logic control_logic_1: pin names not known; wires that end beside it: INSTRUCTION, PCSel, RegWEn, ImmSel, BrEq, BrLt, BrUn, ASel, BSel, ALUSel, MemRW, WBSel, CSRSel, CSRWE
  regfile regfile_1 (
    .rs1(INSTRUCTION[19:15]), .rs2(INSTRUCTION[24:20]), .rd(INSTRUCTION[11:7]), .Write_Data(wb_data),
    .RegWEn(RegWEn), .clk(clk), .ra(ra), .sp(sp), .t0(t0), .t1(t1), .t2(t2), .s0(s0), .s1(s1), .a0(a0),
    .Read_Data_1(read_data_1), .Read_Data_2(MEM_WRITE_reg));
  branch_comp branch_comp_1 (.BrData1(read_data_1), .BrData2(MEM_WRITE_reg), .BrUn(BrUn), .BrEq(BrEq), .BrLt(BrLt));
  csr csr_1 (.CSR_address(12'h51e), .CSR_din(csr_din), .CSR_WE(CSRWE), .clk(clk), .tohost(tohost));
  Multiplexer #(.enable("false"), .width(32)) multiplexer_2 (.in0(read_data_1), .in1(imm), .out(csr_din), .sel(CSRSel));
  Multiplexer #(.enable("false"), .width(32)) multiplexer_3 (
    .in0(read_data_1), .in1(PROGRAM_COUNTER), .out(multiplexer_3_out), .sel(ASel));
  Multiplexer #(.enable("false"), .width(32)) multiplexer_4 (
    .in0(MEM_WRITE_reg), .in1(imm), .out(multiplexer_4_out), .sel(BSel));
  alu alu_1 (.Result(MEM_WRITE_ADDRESS), .A(multiplexer_3_out), .B(multiplexer_4_out), .ALUSel(ALUSel));  // open: out_5
  Multiplexer #(.enable("false"), .select(2), .width(32)) multiplexer_5 (
    .in0(read_mem), .in1(MEM_WRITE_ADDRESS), .in2(pc_4), .in3(imm), .out(wb_data), .sel(WBSel));
  Comparator #(.width(7)) comparator_1 (.a(INSTRUCTION[6:0]), .b(7'b0000011), .eq(comparator_1_eq));  // open: gt, lt
  Comparator #(.width(3)) comparator_2 (.a(INSTRUCTION[14:12]), .b(3'b000), .eq(comparator_2_eq));  // open: gt, lt
  Comparator #(.width(3)) comparator_3 (.a(INSTRUCTION[14:12]), .b(3'b001), .eq(comparator_3_eq));  // open: gt, lt
  Comparator #(.width(3)) comparator_4 (.a(INSTRUCTION[14:12]), .b(3'b010), .eq(comparator_4_eq));  // open: gt, lt
  Comparator #(.width(7)) comparator_5 (.a(INSTRUCTION[6:0]), .b(7'b0100011), .eq(comparator_5_eq));  // open: gt, lt
  Comparator #(.width(3)) comparator_6 (.a(INSTRUCTION[14:12]), .b(3'b000), .eq(comparator_6_eq));  // open: gt, lt
  Comparator #(.width(3)) comparator_7 (.a(INSTRUCTION[14:12]), .b(3'b001), .eq(comparator_7_eq));  // open: gt, lt
  Comparator #(.width(3)) comparator_8 (.a(INSTRUCTION[14:12]), .b(3'b010), .eq(comparator_8_eq));  // open: gt, lt
  and and_1 (lb, comparator_1_eq, comparator_2_eq);
  and and_2 (lh, comparator_1_eq, comparator_3_eq);
  and and_3 (lw, comparator_1_eq, comparator_4_eq);
  and and_4 (sb, comparator_5_eq, comparator_6_eq);
  and and_5 (sh, comparator_5_eq, comparator_7_eq);
  and and_6 (sw, comparator_5_eq, comparator_8_eq);
  Multiplexer #(.enable("false"), .select(2), .width(4)) multiplexer_6 (
    .in0(4'b0001), .in1(4'b0010), .in2(4'b0100), .in3(4'b1000), .out(multiplexer_6_out),
    .sel(MEM_WRITE_ADDRESS[1:0]));
  Multiplexer #(.enable("false"), .width(4)) multiplexer_7 (
    .in0(4'b0000), .in1(multiplexer_6_out), .out(multiplexer_7_out), .sel(sb));
  Multiplexer #(.enable("false"), .width(4)) multiplexer_8 (
    .in0(4'b0011), .in1(4'b1100), .out(multiplexer_8_out), .sel(MEM_WRITE_ADDRESS[1]));
  Multiplexer #(.enable("false"), .select(2), .width(8)) multiplexer_9 (
    .in0(MEM_READ_DATA[7:0]), .in1(MEM_READ_DATA[15:8]), .in2(MEM_READ_DATA[23:16]),
    .in3(MEM_READ_DATA[31:24]), .out(multiplexer_9_out), .sel(MEM_WRITE_ADDRESS[1:0]));
  Multiplexer #(.enable("false"), .width(32)) multiplexer_10 (
    .in0({{16{1'b0}}, MEM_WRITE_reg[15:0]}), .in1({MEM_WRITE_reg[15:0], {16{1'b0}}}), .out(data_sh),
    .sel(MEM_WRITE_ADDRESS[1]));
  Multiplexer #(.enable("false"), .width(4)) multiplexer_11 (
    .in0(multiplexer_7_out), .in1(multiplexer_8_out), .out(multiplexer_11_out), .sel(sh));
  Multiplexer #(.enable("false"), .width(16)) multiplexer_12 (
    .in0(MEM_READ_DATA[15:0]), .in1(MEM_READ_DATA[31:16]), .out(multiplexer_12_out),
    .sel(MEM_WRITE_ADDRESS[1]));
  Multiplexer #(.enable("false"), .width(4)) multiplexer_13 (
    .in0(multiplexer_11_out), .in1(4'b1111), .out(multiplexer_13_out), .sel(sw));
  Multiplexer #(.enable("false"), .select(2), .width(32)) multiplexer_14 (
    .in0({{24{1'b0}}, MEM_WRITE_reg[7:0]}), .in1({{16{1'b0}}, MEM_WRITE_reg[7:0], {8{1'b0}}}),
    .in2({{8{1'b0}}, MEM_WRITE_reg[7:0], {16{1'b0}}}), .in3({MEM_WRITE_reg[7:0], {24{1'b0}}}),
    .out(multiplexer_14_out), .sel(MEM_WRITE_ADDRESS[1:0]));
  Multiplexer #(.enable("false"), .width(32)) multiplexer_15 (
    .in0({{25{1'b0}}, multiplexer_9_out[6:0]}), .in1({{25{1'b1}}, multiplexer_9_out[6:0]}),
    .out(multiplexer_15_out), .sel(multiplexer_9_out[7]));
  Multiplexer #(.enable("false"), .width(32)) multiplexer_16 (
    .in0({{17{1'b0}}, multiplexer_12_out[14:0]}), .in1({{17{1'b1}}, multiplexer_12_out[14:0]}),
    .out(data_lh), .sel(multiplexer_12_out[15]));
  Multiplexer #(.enable("false"), .width(32)) multiplexer_17 (
    .in0(multiplexer_14_out), .in1(data_sh), .out(multiplexer_17_out), .sel(sh));
  Multiplexer #(.enable("false"), .width(4)) multiplexer_18 (
    .in0(4'b0000), .in1(multiplexer_13_out), .out(MEM_WRITE_ENABLE), .sel(MemRW));
  Multiplexer #(.enable("false"), .width(32)) multiplexer_19 (
    .in0(multiplexer_15_out), .in1(data_lh), .out(multiplexer_19_out), .sel(lh));
  Multiplexer #(.enable("false"), .width(32)) multiplexer_20 (
    .in0(multiplexer_17_out), .in1(MEM_WRITE_reg), .out(MEM_WRITE_DATA), .sel(sw));
  Multiplexer #(.enable("false"), .width(32)) multiplexer_21 (
    .in0(multiplexer_19_out), .in1(MEM_READ_DATA), .out(read_mem), .sel(lw));

  // Other names for the same wires on the sheet: read_data_2[31:0] = MEM_WRITE_reg; w1[7:0] = MEM_WRITE_reg[7:0];
  //   wb1[15:0] = MEM_WRITE_reg[15:0]; w2[7:0] = MEM_WRITE_reg[15:8]; op[6:0] = INSTRUCTION[6:0];
  //   rd[4:0] = INSTRUCTION[11:7]; funct3[2:0] = INSTRUCTION[14:12]; rs1[4:0] = INSTRUCTION[19:15];
  //   csr_add[11:0] = INSTRUCTION[31:20]; rs2[4:0] = INSTRUCTION[24:20]; d1[7:0] = MEM_READ_DATA[7:0];
  //   dd1[15:0] = MEM_READ_DATA[15:0]; d2[7:0] = MEM_READ_DATA[15:8]; d3[7:0] = MEM_READ_DATA[23:16];
  //   dd2[15:0] = MEM_READ_DATA[31:16]; d4[7:0] = MEM_READ_DATA[31:24]; w3[7:0] = MEM_WRITE_reg[23:16];
  //   wb2[15:0] = MEM_WRITE_reg[31:16]; w4[7:0] = MEM_WRITE_reg[31:24]; botsel[1:0] = MEM_WRITE_ADDRESS[1:0];
  //   result[31:0] = MEM_WRITE_ADDRESS; botsel1 = MEM_WRITE_ADDRESS[1]

  // Notes on the sheet:
  //   Output to IMEM
  //   IMEM (do **NOT** move this)
  //   Inputs from IMEM
  //   It is OK to move the PC, RegFile, ALU, MEM, Branch Comp, Imm Gen, and Control Logic to wherever is most convenient for you when constructing your CPU, and to delete this text
  //   Inputs/Outputs for testing. Do **NOT** move these.
  //   csr
  //   Outputs To DMEM
  //   DMEM (do **NOT** move this)
  //   Inputs From DMEM
endmodule
