// Logisim project imm_gen.circ as structural Verilog: 1 circuit, main circuit imm_gen
module imm_gen (
  input  [31:0] inst,
  input  [2:0] ImmSel,
  output [31:0] imm
);

  wire [9:0] demultiplexer_3_out0, demultiplexer_3_out1;
  wire [10:0] demultiplexer_1_out0, demultiplexer_1_out1, demultiplexer_2_out0, demultiplexer_2_out1;
  wire [31:0] Itype, Jtype, SBtype, Stype;

  Demultiplexer #(.enable("false"), .width(11)) demultiplexer_1 (
    .out0(demultiplexer_1_out0), .out1(demultiplexer_1_out1), .in(inst[30:20]), .sel(inst[31]));
  Demultiplexer #(.enable("false"), .width(11)) demultiplexer_2 (
    .out0(demultiplexer_2_out0), .out1(demultiplexer_2_out1), .in({inst[30:25], inst[11:7]}), .sel(inst[31]));
  Demultiplexer #(.enable("false"), .width(10)) demultiplexer_3 (
    .out0(demultiplexer_3_out0), .out1(demultiplexer_3_out1), .in({inst[30:25], inst[11:8]}), .sel(inst[31]));
  Multiplexer #(.enable("false"), .width(32)) multiplexer_1 (
    .in0({{21{1'b0}}, demultiplexer_1_out0}), .in1({{21{1'b1}}, demultiplexer_1_out1}), .out(Itype),
    .sel(inst[31]));
  Multiplexer #(.enable("false"), .width(32)) multiplexer_2 (
    .in0({{21{1'b0}}, demultiplexer_2_out0}), .in1({{21{1'b1}}, demultiplexer_2_out1}), .out(Stype),
    .sel(inst[31]));
  Multiplexer #(.enable("false"), .width(32)) multiplexer_3 (
    .in0({{20{1'b0}}, inst[7], demultiplexer_3_out0, 1'b0}),
    .in1({{20{1'b1}}, inst[7], demultiplexer_3_out1, 1'b0}), .out(SBtype), .sel(inst[31]));
  Multiplexer #(.enable("false"), .width(32)) multiplexer_4 (
    .in0({{12{1'b0}}, inst[19:12], inst[20], inst[30:21], 1'b0}),
    .in1({{12{1'b1}}, inst[19:12], inst[20], inst[30:21], 1'b0}), .out(Jtype), .sel(inst[31]));
  Multiplexer #(.enable("false"), .select(3), .width(32)) multiplexer_5 (
    .in0(Itype), .in1(Stype), .in2(SBtype), .in3(Jtype), .in4({inst[31:12], {12{1'b0}}}),
    .in5({{27{1'b0}}, inst[19:15]}), .out(imm), .sel(ImmSel));  // open: in6, in7

  // Other names for the same wires on the sheet: data2[10:0] = {inst[30:25], inst[11:7]}; data[10:0] = inst[30:20];
  //   inst2030[10:0] = inst[30:20]; inst2130[9:0] = inst[30:21]; Jdata[19:1] = {inst[19:12], inst[20], inst[30:21]};
  //   Utype[31:12] = inst[31:12]; data3[9:0] = {inst[30:25], inst[11:8]}; inst1912[7:0] = inst[19:12];
  //   CSRRtype[4:0] = inst[19:15]; sign_flag = inst[31]

  // Notes on the sheet:
  //   INPUTS to your circuit
  //   DON'T CHANGE THE LOCATIONS OF THE INPUTS AND OUTPUTS!
  //   OUTPUT from your circuit
endmodule
