// Logisim project regfile.circ as structural Verilog: 1 circuit, main circuit regfile
module regfile (
  input  [4:0] rs1,
  input  [4:0] rs2,
  input  [4:0] rd,
  input  [31:0] Write_Data,
  input  RegWEn,
  input  clk,
  output [31:0] ra,
  output [31:0] sp,
  output [31:0] t0,
  output [31:0] t1,
  output [31:0] t2,
  output [31:0] s0,
  output [31:0] s1,
  output [31:0] a0,
  output [31:0] Read_Data_1,
  output [31:0] Read_Data_2
);

  wire write_en0, write_en1, write_en2, write_en3, write_en4, write_en5, write_en6, write_en7, write_en8,
       write_en9, write_en10, write_en11, write_en12, write_en13, write_en14, write_en15, write_en16,
       write_en17, write_en18, write_en19, write_en20, write_en21, write_en22, write_en23, write_en24,
       write_en25, write_en26, write_en27, write_en28, write_en29, write_en30, write_en31;
  wire [31:0] a1, a2, a3, a4, a5, a6, a7, gp, s2, s3, s4, s5, s6, s7, s8, s9, s10, s11, t3, t4, t5, t6, tp,
       x0;

  Register #(.width(32)) x2 (.D(Write_Data), .en(write_en2), .clk(clk), .Q(sp));  // open: clr
  Register #(.width(32)) zero (.D({32{1'b0}}), .en(write_en0), .clk(clk), .Q(x0));  // open: clr
  Multiplexer #(.enable("false"), .select(5), .width(32)) multiplexer_1 (
    .in0(x0), .in1(ra), .in2(sp), .in3(gp), .in4(tp), .in5(t0), .in6(t1), .in7(t2), .in8(s0), .in9(s1),
    .in10(a0), .in11(a1), .in12(a2), .in13(a3), .in14(a4), .in15(a5), .in16(a6), .in17(a7), .in18(s2),
    .in19(s3), .in20(s4), .in21(s5), .in22(s6), .in23(s7), .in24(s8), .in25(s9), .in26(s10), .in27(s11),
    .in28(t3), .in29(t4), .in30(t5), .in31(t6), .out(Read_Data_2), .sel(rs2));
  Multiplexer #(.enable("false"), .select(5), .width(32)) multiplexer_2 (
    .in0(x0), .in1(ra), .in2(sp), .in3(gp), .in4(tp), .in5(t0), .in6(t1), .in7(t2), .in8(s0), .in9(s1),
    .in10(a0), .in11(a1), .in12(a2), .in13(a3), .in14(a4), .in15(a5), .in16(a6), .in17(a7), .in18(s2),
    .in19(s3), .in20(s4), .in21(s5), .in22(s6), .in23(s7), .in24(s8), .in25(s9), .in26(s10), .in27(s11),
    .in28(t3), .in29(t4), .in30(t5), .in31(t6), .out(Read_Data_1), .sel(rs1));
  Register #(.width(32)) x1 (.D(Write_Data), .en(write_en1), .clk(clk), .Q(ra));  // open: clr
  Register #(.width(32)) x7 (.D(Write_Data), .en(write_en7), .clk(clk), .Q(t2));  // open: clr
  Register #(.width(32)) x8 (.D(Write_Data), .en(write_en8), .clk(clk), .Q(s0));  // open: clr
  Register #(.width(32)) x9 (.D(Write_Data), .en(write_en9), .clk(clk), .Q(s1));  // open: clr
  Register #(.width(32)) x10 (.D(Write_Data), .en(write_en10), .clk(clk), .Q(a0));  // open: clr
  Register #(.width(32)) x11 (.D(Write_Data), .en(write_en11), .clk(clk), .Q(a1));  // open: clr
  Register #(.width(32)) x3 (.D(Write_Data), .en(write_en3), .clk(clk), .Q(gp));  // open: clr
  Register #(.width(32)) x4 (.D(Write_Data), .en(write_en4), .clk(clk), .Q(tp));  // open: clr
  Register #(.width(32)) x5 (.D(Write_Data), .en(write_en5), .clk(clk), .Q(t0));  // open: clr
  Register #(.width(32)) x6 (.D(Write_Data), .en(write_en6), .clk(clk), .Q(t1));  // open: clr
  Register #(.width(32)) x12 (.D(Write_Data), .en(write_en12), .clk(clk), .Q(a2));  // open: clr
  Register #(.width(32)) x13 (.D(Write_Data), .en(write_en13), .clk(clk), .Q(a3));  // open: clr
  Register #(.width(32)) x14 (.D(Write_Data), .en(write_en14), .clk(clk), .Q(a4));  // open: clr
  Register #(.width(32)) x15 (.D(Write_Data), .en(write_en15), .clk(clk), .Q(a5));  // open: clr
  Demultiplexer #(.enable("false"), .select(5)) demultiplexer_1 (
    .out0(write_en0), .out1(write_en1), .out2(write_en2), .out3(write_en3), .out4(write_en4),
    .out5(write_en5), .out6(write_en6), .out7(write_en7), .out8(write_en8), .out9(write_en9),
    .out10(write_en10), .out11(write_en11), .out12(write_en12), .out13(write_en13), .out14(write_en14),
    .out15(write_en15), .out16(write_en16), .out17(write_en17), .out18(write_en18), .out19(write_en19),
    .out20(write_en20), .out21(write_en21), .out22(write_en22), .out23(write_en23), .out24(write_en24),
    .out25(write_en25), .out26(write_en26), .out27(write_en27), .out28(write_en28), .out29(write_en29),
    .out30(write_en30), .out31(write_en31), .in(RegWEn), .sel(rd));
  Register #(.width(32)) x16 (.D(Write_Data), .en(write_en16), .clk(clk), .Q(a6));  // open: clr
  Register #(.width(32)) x17 (.D(Write_Data), .en(write_en17), .clk(clk), .Q(a7));  // open: clr
  Register #(.width(32)) x18 (.D(Write_Data), .en(write_en18), .clk(clk), .Q(s2));  // open: clr
  Register #(.width(32)) x19 (.D(Write_Data), .en(write_en19), .clk(clk), .Q(s3));  // open: clr
  Register #(.width(32)) x20 (.D(Write_Data), .en(write_en20), .clk(clk), .Q(s4));  // open: clr
  Register #(.width(32)) x21 (.D(Write_Data), .en(write_en21), .clk(clk), .Q(s5));  // open: clr
  Register #(.width(32)) x22 (.D(Write_Data), .en(write_en22), .clk(clk), .Q(s6));  // open: clr
  Register #(.width(32)) x23 (.D(Write_Data), .en(write_en23), .clk(clk), .Q(s7));  // open: clr
  Register #(.width(32)) x24 (.D(Write_Data), .en(write_en24), .clk(clk), .Q(s8));  // open: clr
  Register #(.width(32)) x25 (.D(Write_Data), .en(write_en25), .clk(clk), .Q(s9));  // open: clr
  Register #(.width(32)) x26 (.D(Write_Data), .en(write_en26), .clk(clk), .Q(s10));  // open: clr
  Register #(.width(32)) x27 (.D(Write_Data), .en(write_en27), .clk(clk), .Q(s11));  // open: clr
  Register #(.width(32)) x28 (.D(Write_Data), .en(write_en28), .clk(clk), .Q(t3));  // open: clr
  Register #(.width(32)) x29 (.D(Write_Data), .en(write_en29), .clk(clk), .Q(t4));  // open: clr
  Register #(.width(32)) x30 (.D(Write_Data), .en(write_en30), .clk(clk), .Q(t5));  // open: clr
  Register #(.width(32)) x31 (.D(Write_Data), .en(write_en31), .clk(clk), .Q(t6));  // open: clr

  // Other names for the same wires on the sheet: read_data1[31:0] = Read_Data_1; read_data2[31:0] = Read_Data_2;
  //   read_reg1[4:0] = rs1; read_reg2[4:0] = rs2; write_en = RegWEn; write_reg[4:0] = rd

  // Notes on the sheet:
  //   INPUTS to your circuit
  //   DON'T CHANGE THE LOCATIONS OF THE INPUTS AND OUTPUTS!
  //   These are DEBUG/TEST outputs from your circuit.
  //   OUTPUTS from your circuit
endmodule
